// Logisim project Lab05_Counter.circ as structural Verilog: 7 circuits, main circuit main
module main (
  input  Reset,
  input  [2:0] Sel
);

  wire clk_out;
  wire [3:0] universal_1_out_4;

  Clock #(.highDuration(4), .lowDuration(4)) clk (.out(clk_out));
  Clock sysclk ();  // open: out
  Universal universal_1 (.clk(clk_out), .rst(Reset), .Sel(Sel), .out_4(universal_1_out_4));
  // Probe on universal_1_out_4
  Hex_Digit_Display hex_digit_display_1 (.value(universal_1_out_4));  // open: dp

  // Notes on the sheet:
  //   Aitzhan Kadyrov
  //   Lab 06: Counters
  //   May 02, 2024
endmodule

module asynchronous_up (
  input  clk,
  input  rst,
  output [3:0] Up
);

  wire d_ff_1_qn, d_ff_2_qn, d_ff_3_qn, d_ff_4_qn;

  D_Flip_Flop d_ff_1 (.D(d_ff_1_qn), .clk(clk), .Q(Up[0]), .Qn(d_ff_1_qn), .reset(rst));  // open: preset
  D_Flip_Flop d_ff_2 (.D(d_ff_2_qn), .clk(d_ff_1_qn), .Q(Up[1]), .Qn(d_ff_2_qn), .reset(rst));  // open: preset
  D_Flip_Flop d_ff_3 (.D(d_ff_3_qn), .clk(d_ff_2_qn), .Q(Up[2]), .Qn(d_ff_3_qn), .reset(rst));  // open: preset
  D_Flip_Flop d_ff_4 (.D(d_ff_4_qn), .clk(d_ff_3_qn), .Q(Up[3]), .Qn(d_ff_4_qn), .reset(rst));  // open: preset
endmodule

module asynchronous_down (
  input  clk,
  input  rst,
  output [3:0] Up
);

  wire d_ff_1_qn, d_ff_2_qn, d_ff_3_qn, d_ff_4_qn;

  D_Flip_Flop d_ff_1 (.D(d_ff_1_qn), .clk(clk), .Q(Up[0]), .Qn(d_ff_1_qn), .preset(rst));  // open: reset
  D_Flip_Flop d_ff_2 (.D(d_ff_2_qn), .clk(Up[0]), .Q(Up[1]), .Qn(d_ff_2_qn), .preset(rst));  // open: reset
  D_Flip_Flop d_ff_3 (.D(d_ff_3_qn), .clk(Up[1]), .Q(Up[2]), .Qn(d_ff_3_qn), .preset(rst));  // open: reset
  D_Flip_Flop d_ff_4 (.D(d_ff_4_qn), .clk(Up[2]), .Q(Up[3]), .Qn(d_ff_4_qn), .preset(rst));  // open: reset
endmodule

module asynchronous_decade (
  input  clk,
  input  Reset,
  output [3:0] Up
);

  wire and_1_out, d_ff_1_qn, d_ff_2_qn, d_ff_3_qn, d_ff_4_qn, or_1_out;

  D_Flip_Flop d_ff_1 (.D(d_ff_1_qn), .clk(clk), .Q(Up[0]), .Qn(d_ff_1_qn), .reset(or_1_out));  // open: preset
  or or_1 (or_1_out, Reset, and_1_out);
  D_Flip_Flop d_ff_2 (.D(d_ff_2_qn), .clk(d_ff_1_qn), .Q(Up[1]), .Qn(d_ff_2_qn), .reset(or_1_out));  // open: preset
  D_Flip_Flop d_ff_3 (.D(d_ff_3_qn), .clk(d_ff_2_qn), .Q(Up[2]), .Qn(d_ff_3_qn), .reset(or_1_out));  // open: preset
  D_Flip_Flop d_ff_4 (.D(d_ff_4_qn), .clk(d_ff_3_qn), .Q(Up[3]), .Qn(d_ff_4_qn), .reset(or_1_out));  // open: preset
  and and_1 (and_1_out, Up[3], Up[1]);
endmodule

module synchronous_ring_counter (
  input  clk,
  input  rst,
  output [3:0] Up
);

  D_Flip_Flop d_ff_1 (.D(Up[3]), .clk(clk), .Q(Up[0]), .preset(rst));  // open: Qn, reset
  D_Flip_Flop d_ff_2 (.D(Up[0]), .clk(clk), .Q(Up[1]), .reset(rst));  // open: Qn, preset
  D_Flip_Flop d_ff_3 (.D(Up[1]), .clk(clk), .Q(Up[2]), .reset(rst));  // open: Qn, preset
  D_Flip_Flop d_ff_4 (.D(Up[2]), .clk(clk), .Q(Up[3]), .reset(rst));  // open: Qn, preset
endmodule

module synchronous_johnson_counter (
  input  clk,
  input  rst,
  output [3:0] Up
);

  wire d_ff_4_qn;

  D_Flip_Flop d_ff_1 (.D(d_ff_4_qn), .clk(clk), .Q(Up[0]), .preset(rst));  // open: Qn, reset
  D_Flip_Flop d_ff_2 (.D(Up[0]), .clk(clk), .Q(Up[1]), .reset(rst));  // open: Qn, preset
  D_Flip_Flop d_ff_3 (.D(Up[1]), .clk(clk), .Q(Up[2]), .reset(rst));  // open: Qn, preset
  D_Flip_Flop d_ff_4 (.D(Up[2]), .clk(clk), .Q(Up[3]), .Qn(d_ff_4_qn), .reset(rst));  // open: preset
endmodule

module Universal (
  input  clk,
  input  rst,
  input  [2:0] Sel,
  output [3:0] out_4
);

  wire [3:0] asynchronous_decade_1_up, asynchronous_down_1_up, asynchronous_up_1_up,
       synchronous_johnson_counter_1_up, synchronous_ring_counter_1_up;

  asynchronous_up asynchronous_up_1 (.clk(clk), .rst(rst), .Up(asynchronous_up_1_up));
  asynchronous_down asynchronous_down_1 (.clk(clk), .rst(rst), .Up(asynchronous_down_1_up));
  asynchronous_decade asynchronous_decade_1 (.clk(clk), .Reset(rst), .Up(asynchronous_decade_1_up));
  synchronous_ring_counter synchronous_ring_counter_1 (.clk(clk), .rst(rst), .Up(synchronous_ring_counter_1_up));
  synchronous_johnson_counter synchronous_johnson_counter_1 (
    .clk(clk), .rst(rst), .Up(synchronous_johnson_counter_1_up));
  Multiplexer #(.select(3), .width(4)) multiplexer_1 (
    .in0(asynchronous_up_1_up), .in1(asynchronous_down_1_up), .in2(asynchronous_decade_1_up),
    .in3(synchronous_ring_counter_1_up), .in4(synchronous_johnson_counter_1_up), .in5(4'b0000),
    .in6(4'b0000), .in7(4'b0000), .out(out_4), .sel(Sel));
endmodule
